// Logisim project Home Work 3.circ as structural Verilog
module SR_Latch (
  input  R,
  input  S,
  output Q,
  output minus_Q
);

  nor nor_1 (Q, R, minus_Q);
  nor nor_2 (minus_Q, Q, S);
endmodule

module D_Latch (
  input  CLK,
  input  D,
  output Q,
  output minus_Q
);

  wire and_1_out, and_2_out, not_1_out;

  not not_1 (not_1_out, D);
  and and_1 (and_1_out, CLK, not_1_out);
  and and_2 (and_2_out, CLK, D);
  SR_Latch sr_latch_1 (.R(and_1_out), .S(and_2_out), .Q(Q), .minus_Q(minus_Q));
endmodule

module D_Flip_Flops_rising_edge (
  input  CLK,
  input  D_in,
  output Q_out
);

  wire d_latch_1_q, not_1_out;

  D_Latch d_latch_1 (.CLK(not_1_out), .D(D_in), .Q(d_latch_1_q));  // open: minus_Q
  not not_1 (not_1_out, CLK);
  D_Latch d_latch_2 (.CLK(CLK), .D(d_latch_1_q), .Q(Q_out));  // open: minus_Q
endmodule

module D_Flip_Flops_falling_edge (
  input  CLK,
  input  D_in,
  output Q_out
);

  wire d_latch_1_q, not_1_out;

  not not_1 (not_1_out, CLK);
  D_Latch d_latch_1 (.CLK(CLK), .D(D_in), .Q(d_latch_1_q));  // open: minus_Q
  D_Latch d_latch_2 (.CLK(not_1_out), .D(d_latch_1_q), .Q(Q_out));  // open: minus_Q
endmodule

module Enabled_Flip_Flop (
  input  EN,
  input  CLK,
  input  D,
  output Q
);

  wire multiplexer_1_out;

  Multiplexer #(.enable("false")) multiplexer_1 (.in0(Q), .in1(D), .out(multiplexer_1_out), .sel(EN));
  D_Flip_Flops_rising_edge d_ffs_rising_edge_1 (.CLK(CLK), .D_in(multiplexer_1_out), .Q_out(Q));
endmodule

module Resettable_Flip_Flop (
  input  in_1,
  input  D,
  input  Reset,
  output Q
);

  wire and_1_out, not_1_out;

  not not_1 (not_1_out, Reset);
  and and_1 (and_1_out, D, not_1_out);
  D_Flip_Flops_rising_edge d_ffs_rising_edge_1 (.CLK(in_1), .D_in(and_1_out), .Q_out(Q));
endmodule

module Asynchronously_Resettable_D_Latch (
  input  CLK,
  input  D,
  input  Reset,
  output Q
);

  wire and_1_out, not_1_out, or_1_out;

  not not_1 (not_1_out, Reset);
  or or_1 (or_1_out, Reset, CLK);
  and and_1 (and_1_out, D, not_1_out);
  D_Flip_Flops_rising_edge d_ffs_rising_edge_1 (.CLK(or_1_out), .D_in(and_1_out), .Q_out(Q));
endmodule

module Asynchronously_Resettable_D_Flip_Flop (
  input  CLK,
  input  D,
  input  Reset,
  output Q
);

  wire and_1_out, not_1_out, or_1_out;

  not not_1 (not_1_out, Reset);
  or or_1 (or_1_out, Reset, CLK);
  and and_1 (and_1_out, D, not_1_out);
  D_Flip_Flops_rising_edge d_ffs_rising_edge_1 (.CLK(or_1_out), .D_in(and_1_out), .Q_out(Q));
endmodule

module Synchronously_Settable_D_Flip_Flop (
  input  CLK,
  input  in,
  input  set,
  output out_4
);

  wire or_1_out;

  or or_1 (or_1_out, in, set);
  D_Flip_Flops_rising_edge d_ffs_rising_edge_1 (.CLK(CLK), .D_in(or_1_out), .Q_out(out_4));
endmodule

module Asynchronously_Settable_D_Latch (
  input  CLK,
  input  D,
  input  set,
  output Q
);

  wire and_1_out, and_2_out, not_1_out, not_2_out, or_1_out;

  not not_1 (not_1_out, set);
  not not_2 (not_2_out, D);
  and and_1 (and_1_out, CLK, not_1_out, not_2_out);
  and and_2 (and_2_out, CLK, D);
  or or_1 (or_1_out, and_2_out, set);
  SR_Latch sr_latch_1 (.R(and_1_out), .S(or_1_out), .Q(Q));  // open: minus_Q
endmodule

module Asynchronously_Settable_D_Flip_Flop (
  input  CLK,
  input  D_in,
  input  set,
  output Q_out
);

  wire asynchronously_settable_d_latch_1_q, not_1_out;

  not not_1 (not_1_out, CLK);
  Asynchronously_Settable_D_Latch asynchronously_settable_d_latch_1 (
    .CLK(not_1_out), .D(D_in), .set(set), .Q(asynchronously_settable_d_latch_1_q));
  Asynchronously_Settable_D_Latch asynchronously_settable_d_latch_2 (
    .CLK(CLK), .D(asynchronously_settable_d_latch_1_q), .set(set), .Q(Q_out));
endmodule

module D_Latch_in_Logisim (
  input  CLK,
  input  en,
  input  in,
  input  _0,
  input  _1,
  output out_6
);

  wire and_1_out, asynchronously_settable_d_latch_1_q, multiplexer_1_out;

  and and_1 (and_1_out, CLK, en);
  Asynchronously_Settable_D_Latch asynchronously_settable_d_latch_1 (
    .CLK(and_1_out), .D(in), .set(1'b0), .Q(asynchronously_settable_d_latch_1_q));
  Multiplexer #(.enable("false")) multiplexer_1 (
    .in0(asynchronously_settable_d_latch_1_q), .in1(1'b0), .out(multiplexer_1_out), .sel(_0));
  Multiplexer #(.enable("false")) multiplexer_2 (.in0(multiplexer_1_out), .in1(1'b1), .out(out_6), .sel(_1));
endmodule

module _4_bit_register (
  input  CLK,
  input  [3:0] D,
  output [3:0] out_3
);

  D_Flip_Flops_rising_edge d_ffs_rising_edge_1 (.CLK(CLK), .D_in(D[0]), .Q_out(out_3[0]));
  D_Flip_Flops_rising_edge d_ffs_rising_edge_2 (.CLK(CLK), .D_in(D[1]), .Q_out(out_3[1]));
  D_Flip_Flops_rising_edge d_ffs_rising_edge_3 (.CLK(CLK), .D_in(D[2]), .Q_out(out_3[2]));
  D_Flip_Flops_rising_edge d_ffs_rising_edge_4 (.CLK(CLK), .D_in(D[3]), .Q_out(out_3[3]));
endmodule

module Scheme_13 (
  input  Cin,
  input  [7:0] A,
  input  [7:0] B,
  input  en,
  input  CLK,
  output [7:0] out_6,
  output [7:0] out_7,
  output [7:0] out_8
);

  wire undriven;
  wire [7:0] register_1_q;

  assign out_6 = A | B;  // OR_Gate or_1, 8 bits wide
  Adder adder_1 (.a(out_6), .b(out_8), .out(out_7), .cin(Cin));  // open: cout
  Register register_1 (.D(out_7), .en(en), .Q(register_1_q), .clk(CLK), .clr(undriven));
  Register register_2 (.D(register_1_q), .en(en), .Q(out_8), .clk(CLK));  // open: clr
endmodule

module Scheme_14 (
  input  [7:0] I,
  output [7:0] O
);

  wire button_1_out, clock_1_out;
  wire [7:0] adder_1_out, multiplexer_1_out, not_1_out;

  Button button_1 (.out(button_1_out));
  Clock clock_1 (.out(clock_1_out));
  assign not_1_out = ~I;  // NOT_Gate not_1, 8 bits wide
  Multiplexer #(.width(8), .enable("false")) multiplexer_1 (
    .in0(I), .in1(not_1_out), .out(multiplexer_1_out), .sel(button_1_out));
  Adder adder_1 (.a(multiplexer_1_out), .b(O), .out(adder_1_out), .cin(button_1_out));  // open: cout
  Register register_1 (.D(adder_1_out), .Q(O), .clk(clock_1_out));  // open: en, clr
endmodule

module Scheme_15 (
);

  D_Flip_Flop d_ff_1 ();  // open: clk, D, Q, Qn, preset, en, reset
endmodule

module RAM8 (
  input  CLK,
  input  [15:0] in,
  input  in_3,
  input  [2:0] address,
  output [15:0] out_5
);

  wire demultiplexer_1_out0, demultiplexer_1_out1, demultiplexer_1_out2, demultiplexer_1_out3,
       demultiplexer_1_out4, demultiplexer_1_out5, demultiplexer_1_out6, demultiplexer_1_out7;
  wire [15:0] register_1_q, register_2_q, register_3_q, register_4_q, register_5_q, register_6_q,
       register_7_q, register_8_q;

  Demultiplexer #(.select(3)) demultiplexer_1 (
    .out0(demultiplexer_1_out0), .out1(demultiplexer_1_out1), .out2(demultiplexer_1_out2),
    .out3(demultiplexer_1_out3), .out4(demultiplexer_1_out4), .out5(demultiplexer_1_out5),
    .out6(demultiplexer_1_out6), .out7(demultiplexer_1_out7), .in(in_3), .sel(address));  // open: en
  Register #(.width(16)) register_1 (.D(in), .en(demultiplexer_1_out0), .Q(register_1_q), .clk(CLK));  // open: clr
  Register #(.width(16)) register_2 (.D(in), .en(demultiplexer_1_out1), .Q(register_2_q), .clk(CLK));  // open: clr
  Register #(.width(16)) register_3 (.D(in), .en(demultiplexer_1_out2), .Q(register_3_q), .clk(CLK));  // open: clr
  Register #(.width(16)) register_4 (.D(in), .en(demultiplexer_1_out3), .Q(register_4_q), .clk(CLK));  // open: clr
  Register #(.width(16)) register_5 (.D(in), .en(demultiplexer_1_out4), .Q(register_5_q), .clk(CLK));  // open: clr
  Register #(.width(16)) register_6 (.D(in), .en(demultiplexer_1_out5), .Q(register_6_q), .clk(CLK));  // open: clr
  Register #(.width(16)) register_7 (.D(in), .en(demultiplexer_1_out6), .Q(register_7_q), .clk(CLK));  // open: clr
  Register #(.width(16)) register_8 (.D(in), .en(demultiplexer_1_out7), .Q(register_8_q), .clk(CLK));  // open: clr
  Multiplexer #(.select(3), .width(16), .enable("false")) multiplexer_1 (
    .in0(register_1_q), .in1(register_2_q), .in2(register_3_q), .in3(register_4_q), .in4(register_5_q),
    .in5(register_6_q), .in6(register_7_q), .in7(register_8_q), .out(out_5), .sel(address));
endmodule

module RAM64 (
  input  CLK,
  input  [15:0] in,
  input  in_3,
  input  [5:0] in_4,
  output [15:0] out_5
);

  wire demultiplexer_1_out0, demultiplexer_1_out1, demultiplexer_1_out2, demultiplexer_1_out3,
       demultiplexer_1_out4, demultiplexer_1_out5, demultiplexer_1_out6, demultiplexer_1_out7;
  wire [15:0] ram8_1_out_5, ram8_2_out_5, ram8_3_out_5, ram8_4_out_5, ram8_5_out_5, ram8_6_out_5,
       ram8_7_out_5, ram8_8_out_5;

  Demultiplexer #(.select(3), .enable("false")) demultiplexer_1 (
    .out0(demultiplexer_1_out0), .out1(demultiplexer_1_out1), .out2(demultiplexer_1_out2),
    .out3(demultiplexer_1_out3), .out4(demultiplexer_1_out4), .out5(demultiplexer_1_out5),
    .out6(demultiplexer_1_out6), .out7(demultiplexer_1_out7), .in(in_3), .sel(in_4[2:0]));
  RAM8 ram8_1 (.CLK(CLK), .in(in), .address(in_4[5:3]), .out_5(ram8_1_out_5), .in_3(demultiplexer_1_out0));
  RAM8 ram8_2 (.CLK(CLK), .in(in), .address(in_4[5:3]), .out_5(ram8_2_out_5), .in_3(demultiplexer_1_out1));
  RAM8 ram8_3 (.CLK(CLK), .in(in), .address(in_4[5:3]), .out_5(ram8_3_out_5), .in_3(demultiplexer_1_out2));
  RAM8 ram8_4 (.CLK(CLK), .in(in), .address(in_4[5:3]), .out_5(ram8_4_out_5), .in_3(demultiplexer_1_out3));
  RAM8 ram8_5 (.CLK(CLK), .in(in), .address(in_4[5:3]), .out_5(ram8_5_out_5), .in_3(demultiplexer_1_out4));
  RAM8 ram8_6 (.CLK(CLK), .in(in), .address(in_4[5:3]), .out_5(ram8_6_out_5), .in_3(demultiplexer_1_out5));
  RAM8 ram8_7 (.CLK(CLK), .in(in), .address(in_4[5:3]), .out_5(ram8_7_out_5), .in_3(demultiplexer_1_out6));
  RAM8 ram8_8 (.CLK(CLK), .in(in), .address(in_4[5:3]), .out_5(ram8_8_out_5), .in_3(demultiplexer_1_out7));
  Multiplexer #(.select(3), .width(16), .enable("false")) multiplexer_1 (
    .in0(ram8_1_out_5), .in1(ram8_2_out_5), .in2(ram8_3_out_5), .in3(ram8_4_out_5), .in4(ram8_5_out_5),
    .in5(ram8_6_out_5), .in6(ram8_7_out_5), .in7(ram8_8_out_5), .out(out_5), .sel(in_4[2:0]));

  // Other names for the same wires on the sheet: A[15:0] = in
endmodule

module PC (
  input  reset,
  input  load,
  input  inc,
  input  [7:0] in,
  input  CLK,
  output [7:0] out_6
);

  wire Inc_t, Load_t, not_1_out, not_2_out, not_3_out;
  wire [7:0] adder_1_out, multiplexer_1_out, multiplexer_2_out;

  Multiplexer #(.width(8), .enable("false")) multiplexer_1 (
    .in0(out_6), .in1(in), .out(multiplexer_1_out), .sel(Load_t));
  not not_1 (not_1_out, reset);
  not not_2 (not_2_out, reset);
  not not_3 (not_3_out, load);
  Adder adder_1 (.a(multiplexer_1_out), .b(8'h1), .out(adder_1_out));  // open: cin, cout
  and and_1 (Load_t, not_1_out, load);
  and and_2 (Inc_t, not_2_out, not_3_out, inc);
  Multiplexer #(.width(8), .enable("false")) multiplexer_2 (
    .in0(multiplexer_1_out), .in1(adder_1_out), .out(multiplexer_2_out), .sel(Inc_t));
  Register register_1 (.D(multiplexer_2_out), .Q(out_6), .clk(CLK), .clr(reset));  // open: en
endmodule

module HalfAdder (
  input  a,
  input  b,
  output sum,
  output carry
);

  xor xor_1 (sum, a, b);
  and and_1 (carry, a, b);
endmodule

module FullAdder (
  input  a,
  input  b,
  input  c,
  output sum,
  output carry
);

  wire halfadder_1_carry, halfadder_1_sum, halfadder_2_carry;

  HalfAdder halfadder_1 (.a(a), .b(b), .sum(halfadder_1_sum), .carry(halfadder_1_carry));
  HalfAdder halfadder_2 (.a(halfadder_1_sum), .b(c), .sum(sum), .carry(halfadder_2_carry));
  or or_1 (carry, halfadder_1_carry, halfadder_2_carry);
endmodule

module CPA (
  input  [3:0] a,
  input  [3:0] b,
  input  c,
  output [3:0] sum,
  output carry
);

  wire fulladder_1_carry, fulladder_2_carry, fulladder_3_carry;

  FullAdder fulladder_1 (.a(a[0]), .b(b[0]), .c(c), .sum(sum[0]), .carry(fulladder_1_carry));
  FullAdder fulladder_2 (.a(a[1]), .b(b[1]), .c(fulladder_1_carry), .sum(sum[1]), .carry(fulladder_2_carry));
  FullAdder fulladder_3 (.a(a[2]), .b(b[2]), .c(fulladder_2_carry), .sum(sum[2]), .carry(fulladder_3_carry));
  FullAdder fulladder_4 (.a(a[3]), .b(b[3]), .c(fulladder_3_carry), .sum(sum[3]), .carry(carry));
endmodule
