// Logisim project RGR.circ as structural Verilog: 1 circuit, main circuit main
module main (
  input  a,
  input  b,
  input  c,
  input  d,
  output x
);

  wire and_1_out, and_2_out, and_3_out, and_4_out, not_1_out, not_2_out, not_3_out, not_4_out, not_5_out,
       not_6_out;

  not not_1 (not_1_out, a);
  not not_2 (not_2_out, b);
  and and_1 (and_1_out, not_1_out, not_2_out, not_3_out);
  not not_3 (not_3_out, d);
  not not_4 (not_4_out, a);
  and and_2 (and_2_out, not_4_out, not_5_out);
  not not_5 (not_5_out, c);
  and and_3 (and_3_out, b, c, d);
  and and_4 (and_4_out, a, not_6_out, d);
  not not_6 (not_6_out, b);
  or or_1 (x, and_1_out, and_2_out, and_3_out, and_4_out);
endmodule
