// Logisim project RGR2.circ as structural Verilog
module MureBin (
  input  in,
  output out_2
);

  wire and_1_out, and_2_out, and_3_out, and_4_out, and_5_out, clock_1_out, d_ff_2_q, d_ff_3_q, not_1_out,
       not_2_out, not_3_out, not_4_out, not_5_out, or_1_out, or_2_out;

  Clock clock_1 (.out(clock_1_out));
  and and_1 (and_1_out, in, d_ff_2_q, d_ff_3_q);
  not not_1 (not_1_out, in);
  not not_2 (not_2_out, d_ff_2_q);
  not not_3 (not_3_out, d_ff_3_q);
  not not_4 (not_4_out, d_ff_2_q);
  not not_5 (not_5_out, d_ff_3_q);
  and and_2 (and_2_out, not_1_out, not_2_out, d_ff_3_q);
  and and_3 (and_3_out, in, d_ff_2_q, not_3_out);
  and and_4 (and_4_out, in, not_4_out);
  and and_5 (and_5_out, in, not_5_out);
  or or_1 (or_1_out, and_2_out, and_3_out);
  or or_2 (or_2_out, and_4_out, and_5_out);
  D_Flip_Flop d_ff_1 (.clk(clock_1_out), .D(and_1_out), .Q(out_2));  // open: Qn, preset, en, reset
  D_Flip_Flop d_ff_2 (.clk(clock_1_out), .D(or_1_out), .Q(d_ff_2_q));  // open: Qn, preset, en, reset
  D_Flip_Flop d_ff_3 (.clk(clock_1_out), .D(or_2_out), .Q(d_ff_3_q));  // open: Qn, preset, en, reset
endmodule

module MureStraight (
  input  in,
  output out_2
);

  wire and_1_out, and_2_out, and_3_out, and_4_out, and_5_out, clock_1_out, d_ff_2_q, d_ff_3_q, d_ff_4_q,
       not_1_out, not_2_out, not_3_out, not_4_out, not_5_out;

  Clock clock_1 (.out(clock_1_out));
  and and_1 (and_1_out, in, d_ff_2_q);
  and and_2 (and_2_out, in, d_ff_3_q);
  not not_1 (not_1_out, in);
  not not_2 (not_2_out, d_ff_2_q);
  not not_3 (not_3_out, d_ff_3_q);
  not not_4 (not_4_out, in);
  not not_5 (not_5_out, d_ff_4_q);
  and and_3 (and_3_out, not_1_out, d_ff_4_q);
  and and_4 (and_4_out, in, not_2_out, not_3_out);
  and and_5 (and_5_out, not_4_out, not_5_out);
  D_Flip_Flop d_ff_1 (.clk(clock_1_out), .D(and_1_out), .Q(out_2));  // open: Qn, preset, en, reset
  D_Flip_Flop d_ff_2 (.clk(clock_1_out), .D(and_2_out), .Q(d_ff_2_q));  // open: Qn, preset, en, reset
  D_Flip_Flop d_ff_3 (.clk(clock_1_out), .D(and_3_out), .Q(d_ff_3_q));  // open: Qn, preset, en, reset
  D_Flip_Flop d_ff_4 (.clk(clock_1_out), .D(and_4_out), .Q(d_ff_4_q));  // open: Qn, preset, en, reset
  D_Flip_Flop d_ff_5 (.clk(clock_1_out), .D(and_5_out));  // open: Q, Qn, preset, en, reset
endmodule

module MilleBin (
  input  in,
  output out_2
);

  wire and_1_out, and_2_out, and_3_out, and_4_out, clock_1_out, d_ff_1_q, d_ff_2_q, not_1_out, not_2_out,
       not_3_out, not_4_out, not_5_out, or_1_out, or_2_out;

  Clock clock_1 (.out(clock_1_out));
  not not_1 (not_1_out, in);
  not not_2 (not_2_out, d_ff_1_q);
  not not_3 (not_3_out, d_ff_2_q);
  not not_4 (not_4_out, d_ff_1_q);
  not not_5 (not_5_out, d_ff_2_q);
  and and_1 (and_1_out, not_1_out, not_2_out, d_ff_2_q);
  and and_2 (and_2_out, in, d_ff_1_q, not_3_out);
  and and_3 (and_3_out, in, not_4_out);
  and and_4 (and_4_out, in, not_5_out);
  D_Flip_Flop d_ff_1 (.clk(clock_1_out), .D(or_1_out), .Q(d_ff_1_q));  // open: Qn, preset, en, reset
  or or_1 (or_1_out, and_1_out, and_2_out);
  D_Flip_Flop d_ff_2 (.clk(clock_1_out), .D(or_2_out), .Q(d_ff_2_q));  // open: Qn, preset, en, reset
  or or_2 (or_2_out, and_3_out, and_4_out);
  and and_5 (out_2, in, d_ff_2_q, d_ff_1_q);
endmodule

module MilleStraight (
  input  in,
  output out_2
);

  wire and_1_out, and_2_out, and_3_out, and_4_out, clock_1_out, d_ff_1_q, d_ff_2_q, d_ff_3_q, not_1_out,
       not_2_out, not_3_out, not_4_out, not_5_out, or_1_out;

  Clock clock_1 (.out(clock_1_out));
  and and_1 (and_1_out, in, d_ff_2_q);
  not not_1 (not_1_out, in);
  not not_2 (not_2_out, d_ff_1_q);
  not not_3 (not_3_out, d_ff_2_q);
  not not_4 (not_4_out, in);
  not not_5 (not_5_out, d_ff_3_q);
  and and_2 (and_2_out, not_1_out, d_ff_3_q);
  and and_3 (and_3_out, in, not_2_out, not_3_out);
  and and_4 (and_4_out, not_4_out, not_5_out);
  or or_1 (or_1_out, and_4_out, d_ff_1_q);
  D_Flip_Flop d_ff_1 (.clk(clock_1_out), .D(and_1_out), .Q(d_ff_1_q));  // open: Qn, preset, en, reset
  D_Flip_Flop d_ff_2 (.clk(clock_1_out), .D(and_2_out), .Q(d_ff_2_q));  // open: Qn, preset, en, reset
  D_Flip_Flop d_ff_3 (.clk(clock_1_out), .D(and_3_out), .Q(d_ff_3_q));  // open: Qn, preset, en, reset
  D_Flip_Flop d_ff_4 (.clk(clock_1_out), .D(or_1_out));  // open: Q, Qn, preset, en, reset
  and and_5 (out_2, in, d_ff_1_q);
endmodule
